# Fritzing sketch grove_4digit_display (saved by Fritzing 0.9.3b)

parts:
  XIAO_ESP32C6 = prefix0000
  Grove_4-Digit_Display_(TM1637) = Grove 4 Digit Display

nets:
  N1: XIAO_ESP32C6.connector1, Grove_4-Digit_Display_(TM1637).DIO
  N2: XIAO_ESP32C6.connector2, Grove_4-Digit_Display_(TM1637).CLK
  N3: XIAO_ESP32C6.connector12, Grove_4-Digit_Display_(TM1637).GND
  N4: XIAO_ESP32C6.connector13, Grove_4-Digit_Display_(TM1637).VCC
