# Fritzing sketch grove_accelerometer (saved by Fritzing 0.9.3b)

parts:
  Grove_Shield_for_XIAO_(stacks_onto_XIAO_headers) = prefixIEWFY5DS
  Grove_3-Axis_Accelerometer_(LIS3DHTR) = Grove 3 Axis Digital Accelerometer 16g

nets:
  N1: Grove_Shield_for_XIAO_(stacks_onto_XIAO_headers).connector8, Grove_3-Axis_Accelerometer_(LIS3DHTR).SDA
  N2: Grove_Shield_for_XIAO_(stacks_onto_XIAO_headers).connector10, Grove_3-Axis_Accelerometer_(LIS3DHTR).SCL
  N3: Grove_Shield_for_XIAO_(stacks_onto_XIAO_headers).connector22, Grove_3-Axis_Accelerometer_(LIS3DHTR).VCC
  N4: Grove_Shield_for_XIAO_(stacks_onto_XIAO_headers).connector24, Grove_3-Axis_Accelerometer_(LIS3DHTR).GND
