# Fritzing sketch grove_button (saved by Fritzing 0.9.3b)

parts:
  Grove_Shield_for_XIAO_(stacks_onto_XIAO_headers) = prefixIEWFY5DS
  Grove_Button = Grove Button
  Grove_LED_(placeholder_art_—_Fritzing_has_no_real_Grove_LED_part;_pinout_GND/VCC/SIG_is_correct) = Grove Light Sensor

nets:
  N1: Grove_Shield_for_XIAO_(stacks_onto_XIAO_headers).connector2, Grove_Button.SIG
  N2: Grove_Shield_for_XIAO_(stacks_onto_XIAO_headers).connector14, Grove_LED_(placeholder_art_—_Fritzing_has_no_real_Grove_LED_part;_pinout_GND/VCC/SIG_is_correct).SIG
  VCC: Grove_Shield_for_XIAO_(stacks_onto_XIAO_headers).connector22, Grove_Button.VCC, Grove_LED_(placeholder_art_—_Fritzing_has_no_real_Grove_LED_part;_pinout_GND/VCC/SIG_is_correct).VCC
  GND: Grove_Shield_for_XIAO_(stacks_onto_XIAO_headers).connector24, Grove_Button.GND, Grove_LED_(placeholder_art_—_Fritzing_has_no_real_Grove_LED_part;_pinout_GND/VCC/SIG_is_correct).GND
