# Fritzing sketch grove_light_sensor (saved by Fritzing 0.9.3b)

parts:
  Grove_Shield_for_XIAO_(stacks_onto_XIAO_headers) = prefixIEWFY5DS
  Grove_Light_Sensor = Grove Light Sensor
  Grove_LED_(placeholder_art_—_Fritzing_has_no_real_Grove_LED_part;_pinout_GND/VCC/SIG_is_correct) = Grove Light Sensor

nets:
  N1: Grove_Shield_for_XIAO_(stacks_onto_XIAO_headers).connector0, Grove_Light_Sensor.SIG
  N2: Grove_Shield_for_XIAO_(stacks_onto_XIAO_headers).connector14, Grove_LED_(placeholder_art_—_Fritzing_has_no_real_Grove_LED_part;_pinout_GND/VCC/SIG_is_correct).SIG
  VCC: Grove_Shield_for_XIAO_(stacks_onto_XIAO_headers).connector22, Grove_Light_Sensor.VCC, Grove_LED_(placeholder_art_—_Fritzing_has_no_real_Grove_LED_part;_pinout_GND/VCC/SIG_is_correct).VCC
  GND: Grove_Shield_for_XIAO_(stacks_onto_XIAO_headers).connector24, Grove_Light_Sensor.GND, Grove_LED_(placeholder_art_—_Fritzing_has_no_real_Grove_LED_part;_pinout_GND/VCC/SIG_is_correct).GND
