# Fritzing sketch grove_oled (saved by Fritzing 0.9.3b)

parts:
  Grove_Shield_for_XIAO_(stacks_onto_XIAO_headers) = prefixIEWFY5DS
  Grove_OLED_128x96 = Grove OLED 128x96

nets:
  N1: Grove_Shield_for_XIAO_(stacks_onto_XIAO_headers).connector8, Grove_OLED_128x96.SDA
  N2: Grove_Shield_for_XIAO_(stacks_onto_XIAO_headers).connector10, Grove_OLED_128x96.SCL
  N3: Grove_Shield_for_XIAO_(stacks_onto_XIAO_headers).connector22, Grove_OLED_128x96.VCC
  N4: Grove_Shield_for_XIAO_(stacks_onto_XIAO_headers).connector24, Grove_OLED_128x96.GND
