# Fritzing sketch grove_rgb_stick (saved by Fritzing 1.0.6)

parts:
  XIAO_ESP32C6 = XIAO ESP32C6 [part_number=" XIAO ESP32C6"]
  Grove_RGB_LED_Stick_15x_WS2813_Mini_(placeholder_art_—_closest_real_Fritzing_part_is_the_Grove_Chainable_RGB_LED;_wire_only_DIN/GND/VCC_ignore_its_CI/CO_chain-out_pins) = Grove Chainable RGB LED

nets:
  N1: XIAO_ESP32C6.D7, Grove_RGB_LED_Stick_15x_WS2813_Mini_(placeholder_art_—_closest_real_Fritzing_part_is_the_Grove_Chainable_RGB_LED;_wire_only_DIN/GND/VCC_ignore_its_CI/CO_chain-out_pins).DI
  GND: XIAO_ESP32C6.GND, Grove_RGB_LED_Stick_15x_WS2813_Mini_(placeholder_art_—_closest_real_Fritzing_part_is_the_Grove_Chainable_RGB_LED;_wire_only_DIN/GND/VCC_ignore_its_CI/CO_chain-out_pins).GND
  5V: XIAO_ESP32C6.5V, Grove_RGB_LED_Stick_15x_WS2813_Mini_(placeholder_art_—_closest_real_Fritzing_part_is_the_Grove_Chainable_RGB_LED;_wire_only_DIN/GND/VCC_ignore_its_CI/CO_chain-out_pins).VCC

custom parts:
  XIAO ESP32C6: XIAO ESP32C6 is a cost-effective MCU based on Espressif’s ESP32-C6. This compact MCU excels in Matter-compliant smart home applications with its support for various wireless connectivity (2.4GHz Wi-Fi 6, BLE 5.0, Zigbee, and Thread). Designed with the thumb-size footprint and a single-sided mount of the XIAO Series, it's perfect for space-limited projects. Encrypted on the chip, the XIAO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
  Grove Chainable RGB LED: A chainable RGB LED
