# Fritzing sketch grove_temp_humidity (saved by Fritzing 0.9.3b)

parts:
  Grove_Shield_for_XIAO_(stacks_onto_XIAO_headers) = prefixIEWFY5DS
  Grove_AHT20_Temperature_&_Humidity_Sensor_(placeholder_—_no_real_Fritzing_part_exists;_shown_with_a_generic_Grove_I2C_4-pin_footprint_GND/VCC/SDA/SCL) = Grove OLED 128x96

nets:
  N1: Grove_Shield_for_XIAO_(stacks_onto_XIAO_headers).connector8, Grove_AHT20_Temperature_&_Humidity_Sensor_(placeholder_—_no_real_Fritzing_part_exists;_shown_with_a_generic_Grove_I2C_4-pin_footprint_GND/VCC/SDA/SCL).SDA
  N2: Grove_Shield_for_XIAO_(stacks_onto_XIAO_headers).connector10, Grove_AHT20_Temperature_&_Humidity_Sensor_(placeholder_—_no_real_Fritzing_part_exists;_shown_with_a_generic_Grove_I2C_4-pin_footprint_GND/VCC/SDA/SCL).SCL
  N3: Grove_Shield_for_XIAO_(stacks_onto_XIAO_headers).connector22, Grove_AHT20_Temperature_&_Humidity_Sensor_(placeholder_—_no_real_Fritzing_part_exists;_shown_with_a_generic_Grove_I2C_4-pin_footprint_GND/VCC/SDA/SCL).VCC
  N4: Grove_Shield_for_XIAO_(stacks_onto_XIAO_headers).connector24, Grove_AHT20_Temperature_&_Humidity_Sensor_(placeholder_—_no_real_Fritzing_part_exists;_shown_with_a_generic_Grove_I2C_4-pin_footprint_GND/VCC/SDA/SCL).GND
